// Logisim project main.circ as structural Verilog: 4 circuits, main circuit main
module main (
  input  in_1,
  input  reset
);

  wire add, addi, and_1_out, and_2_out, clock_1_out, comparator_1_eq, comparator_1_gt, comparator_2_eq,
       comparator_2_lt, decoder_1_out1, decoder_1_out2, decoder_1_out3, decoder_1_out4, decoder_1_out5,
       decoder_1_out6, decoder_1_out7, decoder_1_out8, decoder_1_out9, decoder_1_out10, decoder_1_out11,
       decoder_1_out12, decoder_1_out13, decoder_1_out14, decoder_1_out15, decoder_2_out0, decoder_2_out1,
       decoder_2_out2, decoder_2_out3, jalr, lbu, lui, lw, or_1_out, or_2_out, or_3_out, or_4_out, or_5_out,
       or_6_out, or_7_out, or_8_out, sb, sw;
  wire [0:0] adder_3_out;
  wire [2:0] data_select, fuct3;
  wire [4:0] rd, rs1, rs2;
  wire [6:0] imm_7;
  wire [7:0] multiplexer_10_out;
  wire [11:0] imm_12;
  wire [19:0] imm_20;
  wire [23:0] rgb_video_1_p6;
  wire [31:0] add_finish, adder_2_out, addi_finish, bit_extender_1_out, bit_extender_2_out,
       bit_extender_3_out, bit_extender_4_out, demultiplexer_1_out1, demultiplexer_2_out0,
       demultiplexer_2_out1, demultiplexer_2_out2, demultiplexer_2_out3, jarl_rd, lbu_RAM_out, load_addr,
       mem_store_addr, multiplexer_2_out, multiplexer_4_out, multiplexer_5_out, multiplexer_8_out,
       multiplexer_9_out, RAM_out, register_1_q, register_2_q, register_3_q, register_4_q, register_5_q,
       register_6_q, register_7_q, register_8_q, register_9_q, register_10_q, register_11_q, register_12_q,
       register_13_q, register_14_q, register_15_q, register_16_q, register_17_q, rom_1_data, rs1_out,
       rs2_out, store_addr;
  wire [31:1] jalr_finish;

  Multiplexer multiplexer_1 ();  // open: in0, in1, out, sel
  Register #(.trigger("falling"), .width(32)) register_1 (
    .D(multiplexer_2_out), .en(in_1), .clk(clock_1_out), .Q(register_1_q), .clr(reset));
  Clock clock_1 (.out(clock_1_out));
  Multiplexer #(.width(32)) multiplexer_2 (
    .in0(adder_2_out), .in1({jalr_finish, 1'b0}), .out(multiplexer_2_out), .sel(jalr));
  Adder #(.width(32)) adder_1 (.a(register_1_q), .b(32'h4), .out(jarl_rd));  // open: cin, cout
  Comparator #(.width(32)) comparator_1 (
    .a(store_addr), .b(32'h20000000), .gt(comparator_1_gt), .eq(comparator_1_eq));  // open: lt
  Comparator #(.width(32)) comparator_2 (
    .a(store_addr), .b(32'h20040000), .eq(comparator_2_eq), .lt(comparator_2_lt));  // open: gt
  or or_1 (or_1_out, comparator_1_gt, comparator_1_eq);
  or or_2 (or_2_out, comparator_2_eq, comparator_2_lt);
  Adder #(.width(32)) adder_2 (.a(32'h4), .b(register_1_q), .out(adder_2_out));  // open: cin, cout
  and and_1 (and_1_out, or_1_out, or_2_out);
  Demultiplexer #(.width(32)) demultiplexer_1 (
    .out0(mem_store_addr), .out1(demultiplexer_1_out1), .in(store_addr), .sel(and_1_out));
  ROM #(.addrWidth(24), .dataWidth(32)) rom_1 (.addr(register_1_q[25:2]), .data(rom_1_data));
  and and_2 (and_2_out, and_1_out, sw);
  // RGB_Video #(.cursor("No Cursor"), .height(256), .width(256)) rgb_video_1: pin names not known; wires that end beside it: reset, clock_1_out, and_2_out, demultiplexer_1_out1[9:2], demultiplexer_1_out1[17:10], rgb_video_1_p6
  Multiplexer #(.width(24)) multiplexer_3 (.in1(rs2_out[23:0]), .out(rgb_video_1_p6), .sel(sw));  // open: in0
  opcoder_decoder opcoder_decoder_1 (
    .in_1(rom_1_data), .addi(addi), .jalr(jalr), .add(add), .lui(lui), .lw(lw), .lbu(lbu), .sw(sw), .sb(sb));
  data_choose data_choose_1 (
    .in_1(rom_1_data), .imm_12(imm_12), .rs1(rs1), .funct3(fuct3), .rd(rd), .rs2(rs2), .imm_20(imm_20),
    .imm_7(imm_7));
  Multiplexer #(.select(3), .width(32)) multiplexer_4 (
    .in0(addi_finish), .in1(jarl_rd), .in2(add_finish), .in3({imm_20, {12{1'b0}}}), .in4(RAM_out),
    .in5(lbu_RAM_out), .out(multiplexer_4_out), .sel(data_select));  // open: in6, in7
  or or_3 (or_3_out, addi, jalr, add, lui, lw, lbu);
  or or_4 (or_4_out, sb, sw);
  Priority_Encoder priority_encoder_1 (
    .in0(addi), .in1(jalr), .in2(add), .in3(lui), .in4(lw), .in5(lbu), .in6(sw), .in7(sb), .out(data_select));  // open: en_in, gs, en_out
  Decoder #(.select(4)) decoder_1 (
    .out1(decoder_1_out1), .out2(decoder_1_out2), .out3(decoder_1_out3), .out4(decoder_1_out4),
    .out5(decoder_1_out5), .out6(decoder_1_out6), .out7(decoder_1_out7), .out8(decoder_1_out8),
    .out9(decoder_1_out9), .out10(decoder_1_out10), .out11(decoder_1_out11), .out12(decoder_1_out12),
    .out13(decoder_1_out13), .out14(decoder_1_out14), .out15(decoder_1_out15), .sel(rd[3:0]), .en(or_3_out));  // open: out0
  Register #(.trigger("falling"), .width(32)) register_2 (
    .D(multiplexer_4_out), .en(1'b0), .clk(clock_1_out), .Q(register_2_q), .clr(reset));
  Register #(.trigger("falling"), .width(32)) register_3 (
    .D(multiplexer_4_out), .en(decoder_1_out8), .clk(clock_1_out), .Q(register_3_q), .clr(reset));
  assign bit_extender_1_out = {{20{imm_12[11]}}, imm_12};  // Bit_Extender bit_extender_1
  Register #(.trigger("falling"), .width(32)) register_4 (
    .D(multiplexer_4_out), .en(decoder_1_out1), .clk(clock_1_out), .Q(register_4_q), .clr(reset));
  Register #(.trigger("falling"), .width(32)) register_5 (
    .D(multiplexer_4_out), .en(decoder_1_out9), .clk(clock_1_out), .Q(register_5_q), .clr(reset));
  assign bit_extender_2_out = {{20{imm_12[11]}}, imm_12};  // Bit_Extender bit_extender_2
  assign bit_extender_3_out = {{20{imm_12[11]}}, imm_12};  // Bit_Extender bit_extender_3
  Register #(.trigger("falling"), .width(32)) register_6 (
    .D(multiplexer_4_out), .en(decoder_1_out2), .clk(clock_1_out), .Q(register_6_q), .clr(reset));
  Register #(.trigger("falling"), .width(32)) register_7 (
    .D(multiplexer_4_out), .en(decoder_1_out10), .clk(clock_1_out), .Q(register_7_q), .clr(reset));
  Adder #(.width(32)) adder_3 (
    .a(bit_extender_2_out), .b(rs1_out), .out({jalr_finish, adder_3_out[0]}));  // open: cin, cout
  Adder #(.width(32)) adder_4 (.a(rs1_out), .b(rs2_out), .out(add_finish));  // open: cin, cout
  Adder #(.width(32)) adder_5 (.a(rs1_out), .b(bit_extender_3_out), .out(load_addr));  // open: cin, cout
  Register #(.trigger("falling"), .width(32)) register_8 (
    .D(multiplexer_4_out), .en(decoder_1_out3), .clk(clock_1_out), .Q(register_8_q), .clr(reset));
  Register #(.trigger("falling"), .width(32)) register_9 (
    .D(multiplexer_4_out), .en(decoder_1_out11), .clk(clock_1_out), .Q(register_9_q), .clr(reset));
  Adder #(.width(32)) adder_6 (.a(bit_extender_1_out), .b(rs1_out), .out(addi_finish));  // open: cin, cout
  assign bit_extender_4_out = {{20{imm_7[6]}}, {imm_7, rd}};  // Bit_Extender bit_extender_4
  Register #(.trigger("falling"), .width(32)) register_10 (
    .D(multiplexer_4_out), .en(decoder_1_out4), .clk(clock_1_out), .Q(register_10_q), .clr(reset));
  Register #(.trigger("falling"), .width(32)) register_11 (
    .D(multiplexer_4_out), .en(decoder_1_out12), .clk(clock_1_out), .Q(register_11_q), .clr(reset));
  Adder #(.width(32)) adder_7 (.a(bit_extender_4_out), .b(rs1_out), .out(store_addr));  // open: cin, cout
  Register #(.trigger("falling"), .width(32)) register_12 (
    .D(multiplexer_4_out), .en(decoder_1_out5), .clk(clock_1_out), .Q(register_12_q), .clr(reset));
  Register #(.trigger("falling"), .width(32)) register_13 (
    .D(multiplexer_4_out), .en(decoder_1_out13), .clk(clock_1_out), .Q(register_13_q), .clr(reset));
  Register #(.trigger("falling"), .width(32)) register_14 (
    .D(multiplexer_4_out), .en(decoder_1_out6), .clk(clock_1_out), .Q(register_14_q), .clr(reset));
  Register #(.trigger("falling"), .width(32)) register_15 (
    .D(multiplexer_4_out), .en(decoder_1_out14), .clk(clock_1_out), .Q(register_15_q), .clr(reset));
  Register #(.trigger("falling"), .width(32)) register_16 (
    .D(multiplexer_4_out), .en(decoder_1_out7), .clk(clock_1_out), .Q(register_16_q), .clr(reset));
  Register #(.trigger("falling"), .width(32)) register_17 (
    .D(multiplexer_4_out), .en(decoder_1_out15), .clk(clock_1_out), .Q(register_17_q), .clr(reset));
  Multiplexer #(.width(32)) multiplexer_5 (
    .in0(load_addr), .in1(mem_store_addr), .out(multiplexer_5_out), .sel(or_4_out));
  Decoder #(.enable("false"), .select(2)) decoder_2 (
    .out0(decoder_2_out0), .out1(decoder_2_out1), .out2(decoder_2_out2), .out3(decoder_2_out3),
    .sel(store_addr[1:0]));
  Demultiplexer #(.select(2), .width(32)) demultiplexer_2 (
    .out0(demultiplexer_2_out0), .out1(demultiplexer_2_out1), .out2(demultiplexer_2_out2),
    .out3(demultiplexer_2_out3), .in(rs2_out), .sel(store_addr[1:0]));
  Multiplexer #(.select(4), .width(32)) multiplexer_6 (
    .in0(register_2_q), .in1(register_4_q), .in2(register_6_q), .in3(register_8_q), .in4(register_10_q),
    .in5(register_12_q), .in6(register_14_q), .in7(register_16_q), .in8(register_3_q), .in9(register_5_q),
    .in10(register_7_q), .in11(register_9_q), .in12(register_11_q), .in13(register_13_q),
    .in14(register_15_q), .in15(register_17_q), .out(rs1_out), .sel(rs1[3:0]));
  Multiplexer #(.select(4), .width(32)) multiplexer_7 (
    .in0(register_2_q), .in1(register_4_q), .in2(register_6_q), .in3(register_8_q), .in4(register_10_q),
    .in5(register_12_q), .in6(register_14_q), .in7(register_16_q), .in8(register_3_q), .in9(register_5_q),
    .in10(register_7_q), .in11(register_9_q), .in12(register_11_q), .in13(register_13_q),
    .in14(register_15_q), .in15(register_17_q), .out(rs2_out), .sel(rs2[3:0]));
  or or_5 (or_5_out, decoder_2_out3, sw);
  or or_6 (or_6_out, decoder_2_out2, sw);
  or or_7 (or_7_out, decoder_2_out1, sw);
  or or_8 (or_8_out, decoder_2_out0, sw);
  RAM #(.addrWidth(24), .asyncread("true"), .byteenables("byteEnables"), .dataWidth(32), .\type ("nonvolatile")) ram_1 (
    .addr(multiplexer_5_out[25:2]), .we(or_4_out), .oe(1'b1), .clk(clock_1_out), .din(multiplexer_8_out),
    .dout(RAM_out), .be3(or_5_out), .be2(or_6_out), .be1(or_7_out), .be0(or_8_out));
  Multiplexer #(.width(32)) multiplexer_8 (.in0(rs2_out), .in1(multiplexer_9_out), .out(multiplexer_8_out), .sel(sb));
  Multiplexer #(.select(2), .width(32)) multiplexer_9 (
    .in0(demultiplexer_2_out0), .in1({{16{1'b0}}, demultiplexer_2_out1[7:0], {8{1'b0}}}),
    .in2({{8{1'b0}}, demultiplexer_2_out2[7:0], {16{1'b0}}}), .in3({demultiplexer_2_out3[7:0], {24{1'b0}}}),
    .out(multiplexer_9_out), .sel(store_addr[1:0]));
  Multiplexer #(.select(2), .width(8)) multiplexer_10 (
    .in0(RAM_out[7:0]), .in1(RAM_out[15:8]), .in2(RAM_out[23:16]), .in3(RAM_out[31:24]),
    .out(multiplexer_10_out), .sel(load_addr[1:0]));
  assign lbu_RAM_out = {{24{1'b0}}, multiplexer_10_out};  // Bit_Extender bit_extender_5

  // Other names for the same wires on the sheet: lui_finish[31:12] = imm_20

  // Notes on the sheet:
  //   contents of rom_1 (hex, n*v repeats v):
  //   413 52137 10113 10b7 22408093 80e7 fea12823 fe812e23 1437 40840413 ff014183 3401b3 1c183 ff114203
  //   440233 24203 4181b3 ff214203 440233 24203 4181b3 ff314203 440233 24203 4181b3 1237 40020213 320233
  //   24203 ffc12403 420233 420233 410233 a000193 fe312823 9c00193 fe312623 fec22203 20067 8067 ff410113
  //   100513 112423 10b7 21808093 80e7 fec10113 912423 494b7 6b048493 812623 112823 496b7 69068693 48413
  //   48713 fe012823 174183 fe3109a3 ff012183 fe812e23 fe312823 3d437 60040413 ff214203 420233 420233
  //   440233 22203 fe412623 ff114203 420233 420233 440233 22203 fe412423 ff014203 420233 420233 440233
  //   22203 fe412223 fed14183 fea14203 4181b3 fe714203 4181b3 fe312223 fee14183 feb14203 4181b3 fe3102a3
  //   fef14183 fe310323 fe412183 8237 20213 440433 ff314203 420233 420233 440233 22203 ffc12403 4181b3
  //   74503 350533 6a603 270713 468693 fe312a23 fec12423 31237 50020213 feb14183 4181b3 1c183 fe3103a3
  //   fea14183 4181b3 1c183 fe310323 fe914183 4181b3 1c183 fe3102a3 fe814183 4181b3 1c183 fe310223
  //   ff412183 fe412203 450533 150513 fea12823 fe812e23 1437 40840413 ff014183 3401b3 1c183 ff114203
  //   440233 24203 4181b3 ff214203 440233 24203 4181b3 ff314203 440233 24203 4181b3 1237 40020213 320233
  //   24503 ffc12403 e12223 d12023 1800093 80e7 412703 497b7 6c078793 12683 fee12823 fef12623 fe812e23
  //   fe912c23 1437 30040413 ff014183 340233 100193 320023 fec14183 3401b3 18023 24183 ff114483 940233
  //   100493 920023 fed14483 9404b3 48023 24483 9181b3 ff214483 940233 100493 920023 fee14483 9404b3 48023
  //   24483 9181b3 ff314483 940233 100493 920023 fef14483 9404b3 48023 24483 9181b3 1237 40020213 320233
  //   24203 ff812483 ffc12403 420233 420233 410233 37800193 fe312823 e000193 fe312623 fec22203 20067 49737
  //   67070713 72683 fe012823 14c203 fe4108a3 ff012203 4c503 450533 470713 e12023 fe312a23 fed12423 31237
  //   50020213 feb14183 4181b3 1c183 fe3103a3 fea14183 4181b3 1c183 fe310323 fe914183 4181b3 1c183
  //   fe3102a3 fe814183 4181b3 1c183 fe310223 ff412183 fe412203 450533 150513 fea12823 fe812e23 1437
  //   40840413 ff014183 3401b3 1c183 ff114203 440233 24203 4181b3 ff214203 440233 24203 4181b3 ff314203
  //   440233 24203 4181b3 1237 40020213 320233 24503 ffc12403 1800093 80e7 248493 497b7 6c078793 12703
  //   fe912823 fef12623 fe812e23 fe912c23 1437 30040413 ff014183 340233 100193 320023 fec14183 3401b3
  //   18023 24183 ff114483 940233 100493 920023 fed14483 9404b3 48023 24483 9181b3 ff214483 940233 100493
  //   920023 fee14483 9404b3 48023 24483 9181b3 ff314483 940233 100493 920023 fef14483 9404b3 48023 24483
  //   9181b3 1237 40020213 320233 24203 ff812483 ffc12403 420233 420233 410233 55c00193 fe312823 38000193
  //   fe312623 fec22203 20067 244683 144603 344703 444783 494b7 64048493 8*d686b3 fed12823 fec12623 116b7
  //   60068693 fe012223 ff314203 fe4102a3 fef14203 fe410223 fe412203 468233 24203 fe4105a3 ff214203
  //   fe4102a3 fee14203 fe410223 fe412203 468233 24203 fe410523 ff114203 fe4102a3 fed14203 fe410223
  //   fe412203 468233 24203 fe4104a3 ff014203 fe4102a3 fec14203 fe410223 fe412203 468233 24203 fe410423
  //   fe812683 4a503 fe012823 fee10923 fee12423 fe914203 fe4109a3 ff012703 fee12823 fed12623 11737
  //   60070713 fe012223 ff314203 fe4102a3 fef14203 fe410223 fe412203 470233 24203 fe4105a3 ff214203
  //   fe4102a3 fee14203 fe410223 fe412203 470233 24203 fe410523 ff114203 fe4102a3 fed14203 fe410223
  //   fe412203 470233 24203 fe4104a3 ff014203 fe4102a3 fec14203 fe410223 fe412203 470233 24203 fe410423
  //   fe812703 fe012823 fef109a3 ff012783 fef12823 fee12623 117b7 60078793 fe012223 ff314203 fe4102a3
  //   fef14203 fe410223 fe412203 478233 24203 fe4105a3 ff214203 fe4102a3 fee14203 fe410223 fe412203 478233
  //   24203 fe410523 ff114203 fe4102a3 fed14203 fe410223 fe412203 478233 24203 fe4104a3 ff014203 fe4102a3
  //   fec14203 fe410223 fe412203 478233 24203 fe410423 fe812783 fe312a23 fef12423 31237 50020213 feb14183
  //   4181b3 1c183 fe3103a3 fea14183 4181b3 1c183 fe310323 fe914183 4181b3 1c183 fe3102a3 fe814183 4181b3
  //   1c183 fe310223 ff412183 fe412203 450533 150513 fea12823 fe812e23 1437 40840413 ff014183 3401b3 1c183
  //   ff114203 440233 24203 4181b3 ff214203 440233 24203 4181b3 ff314203 440233 24203 4181b3 1237 400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
endmodule

module opcoder_decoder (
  input  [31:0] in_1,
  output addi,
  output jalr,
  output add,
  output lui,
  output lw,
  output lbu,
  output sw,
  output sb
);

  wire comparator_3_eq, comparator_5_eq, comparator_6_eq, comparator_7_eq;
  wire [2:0] multiplexer_1_out, multiplexer_2_out;

  Comparator #(.mode("unsigned"), .width(7)) comparator_1 (.a(in_1[6:0]), .b(7'b0010011), .eq(addi));  // open: gt, lt
  Comparator #(.width(7)) comparator_2 (.a(in_1[6:0]), .b(7'b1100111), .eq(jalr));  // open: gt, lt
  Comparator #(.width(7)) comparator_3 (.a(in_1[6:0]), .b(7'b0110011), .eq(comparator_3_eq));  // open: gt, lt
  Comparator #(.width(7)) comparator_4 (.a(in_1[6:0]), .b(7'b0110111), .eq(lui));  // open: gt, lt
  Comparator #(.width(7)) comparator_5 (.a(in_1[6:0]), .b(7'b0000011), .eq(comparator_5_eq));  // open: gt, lt
  Comparator #(.width(7)) comparator_6 (.a(in_1[6:0]), .b(7'b0100011), .eq(comparator_6_eq));  // open: gt, lt
  Comparator #(.width(3)) comparator_7 (.a(in_1[14:12]), .b(3'b000), .eq(comparator_7_eq));  // open: gt, lt
  Multiplexer #(.width(3)) multiplexer_1 (
    .in0(3'b000), .in1(in_1[14:12]), .out(multiplexer_1_out), .sel(comparator_5_eq));
  Multiplexer #(.width(3)) multiplexer_2 (
    .in0(3'b001), .in1(in_1[14:12]), .out(multiplexer_2_out), .sel(comparator_6_eq));
  Multiplexer multiplexer_3 (.in0(1'b0), .in1(comparator_3_eq), .out(add), .sel(comparator_7_eq));
  Comparator #(.mode("unsigned"), .width(3)) comparator_8 (.a(multiplexer_1_out), .b(3'b010), .eq(lw));  // open: gt, lt
  Comparator #(.mode("unsigned"), .width(3)) comparator_9 (
    .a(multiplexer_1_out), .b(3'b100), .eq(lbu));  // open: gt, lt
  Comparator #(.mode("unsigned"), .width(3)) comparator_10 (
    .a(multiplexer_2_out), .b(3'b010), .eq(sw));  // open: gt, lt
  Comparator #(.mode("unsigned"), .width(3)) comparator_11 (
    .a(multiplexer_2_out), .b(3'b000), .eq(sb));  // open: gt, lt
endmodule

module GPR (
  input  clk,
  input  [31:0] wdata
);

  wire decoder_1_out1, decoder_1_out2, decoder_1_out3, decoder_1_out4, decoder_1_out5, decoder_1_out6,
       decoder_1_out7, decoder_1_out8, decoder_1_out9, decoder_1_out10, decoder_1_out11, decoder_1_out12,
       decoder_1_out13, decoder_1_out14, decoder_1_out15;
  wire [31:0] register_1_q, register_2_q, register_3_q, register_4_q, register_5_q, register_6_q,
       register_7_q, register_8_q, register_9_q, register_10_q, register_11_q, register_12_q, register_13_q,
       register_14_q, register_15_q, register_16_q;

  Decoder #(.select(4)) decoder_1 (
    .out1(decoder_1_out1), .out2(decoder_1_out2), .out3(decoder_1_out3), .out4(decoder_1_out4),
    .out5(decoder_1_out5), .out6(decoder_1_out6), .out7(decoder_1_out7), .out8(decoder_1_out8),
    .out9(decoder_1_out9), .out10(decoder_1_out10), .out11(decoder_1_out11), .out12(decoder_1_out12),
    .out13(decoder_1_out13), .out14(decoder_1_out14), .out15(decoder_1_out15));  // open: out0, sel, en
  Register #(.width(32)) register_1 (.D(wdata), .en(decoder_1_out1), .clk(clk), .Q(register_1_q));  // open: clr
  Register #(.width(32)) register_2 (.D(wdata), .en(decoder_1_out8), .clk(clk), .Q(register_2_q));  // open: clr
  Register #(.width(32)) register_3 (.D(wdata), .en(decoder_1_out1), .clk(clk), .Q(register_3_q));  // open: clr
  Register #(.width(32)) register_4 (.D(wdata), .en(decoder_1_out9), .clk(clk), .Q(register_4_q));  // open: clr
  Register #(.width(32)) register_5 (.D(wdata), .en(decoder_1_out2), .clk(clk), .Q(register_5_q));  // open: clr
  Register #(.width(32)) register_6 (.D(wdata), .en(decoder_1_out10), .clk(clk), .Q(register_6_q));  // open: clr
  Register #(.width(32)) register_7 (.D(wdata), .en(decoder_1_out3), .clk(clk), .Q(register_7_q));  // open: clr
  Register #(.width(32)) register_8 (.D(wdata), .en(decoder_1_out11), .clk(clk), .Q(register_8_q));  // open: clr
  Register #(.width(32)) register_9 (.D(wdata), .en(decoder_1_out4), .clk(clk), .Q(register_9_q));  // open: clr
  Register #(.width(32)) register_10 (.D(wdata), .en(decoder_1_out12), .clk(clk), .Q(register_10_q));  // open: clr
  Register #(.width(32)) register_11 (.D(wdata), .en(decoder_1_out5), .clk(clk), .Q(register_11_q));  // open: clr
  Register #(.width(32)) register_12 (.D(wdata), .en(decoder_1_out13), .clk(clk), .Q(register_12_q));  // open: clr
  Register #(.width(32)) register_13 (.D(wdata), .en(decoder_1_out6), .clk(clk), .Q(register_13_q));  // open: clr
  Register #(.width(32)) register_14 (.D(wdata), .en(decoder_1_out14), .clk(clk), .Q(register_14_q));  // open: clr
  Register #(.width(32)) register_15 (.D(wdata), .en(decoder_1_out7), .clk(clk), .Q(register_15_q));  // open: clr
  Register #(.width(32)) register_16 (.D(wdata), .en(decoder_1_out15), .clk(clk), .Q(register_16_q));  // open: clr
  Multiplexer #(.select(4), .width(32)) multiplexer_1 (
    .in0(register_1_q), .in1(register_3_q), .in2(register_5_q), .in3(register_7_q), .in4(register_9_q),
    .in5(register_11_q), .in6(register_13_q), .in7(register_15_q), .in8(register_2_q), .in9(register_4_q),
    .in10(register_6_q), .in11(register_8_q), .in12(register_10_q), .in13(register_12_q),
    .in14(register_14_q), .in15(register_16_q));  // open: out, sel
  Multiplexer #(.select(4), .width(32)) multiplexer_2 (
    .in0(register_1_q), .in1(register_3_q), .in2(register_5_q), .in3(register_7_q), .in4(register_9_q),
    .in5(register_11_q), .in6(register_13_q), .in7(register_15_q), .in8(register_2_q), .in9(register_4_q),
    .in10(register_6_q), .in11(register_8_q), .in12(register_10_q), .in13(register_12_q),
    .in14(register_14_q), .in15(register_16_q));  // open: out, sel
endmodule

module data_choose (
  input  [31:0] in_1,
  output [11:0] imm_12,
  output [4:0] rs1,
  output [2:0] funct3,
  output [4:0] rd,
  output [4:0] rs2,
  output [19:0] imm_20,
  output [6:0] imm_7
);


  assign funct3 = in_1[14:12];
  assign imm_7 = in_1[31:25];
  assign imm_12 = in_1[31:20];
  assign imm_20 = in_1[31:12];
  assign rd = in_1[11:7];
  assign rs1 = in_1[19:15];
  assign rs2 = in_1[24:20];
endmodule
